# Fritzing sketch simple_hw_setup (saved by Fritzing 0.9.2b)
breadboards: 1

parts:
  Part1 = Arduino Uno (Rev3)
  HM-11 = IC, DIP package, 16 pins [chip_label=HM-11]
  R1 = Resistor [tolerance=±5% resistance=1.8k package=THT]
  R2 = Resistor [tolerance=±5% resistance=3.3k package=THT]

nets:
  N1: Part1.D0/RX, HM-11.pin15
  N2: Part1.D1/TX, R1.Pin_1
  N3: Part1.3V3, HM-11.pin8
  N4: Part1.GND, HM-11.pin5, R2.Pin_1
  N5: HM-11.pin13, R1.Pin_0, R2.Pin_0
